// Logisim project B-10.circ as structural Verilog: 2 circuits, main circuit main
module main (
  input  A,
  input  B,
  input  A_2,
  input  B_2,
  output out_5,
  output out_6
);

  wire not_1_out, not_2_out;

  not not_1 (not_1_out, B);
  not not_2 (not_2_out, B_2);
  _2X1_Mux u_2x1_mux_1 (.S(A), .A(1'b1), .B(not_1_out), .Y(out_5));
  _2X1_Mux u_2x1_mux_2 (.S(A_2), .A(not_2_out), .B(1'b0), .Y(out_6));

  // Notes on the sheet:
  //   1
  //   NAND GATE USING 2X1 MUX
  //   NOR GATE USING 2X1 MUX
endmodule

module _2X1_Mux (
  input  S,
  input  A,
  input  B,
  output Y
);

  wire and_1_out, and_2_out, not_1_out;

  not not_1 (not_1_out, S);
  and and_1 (and_1_out, not_1_out, A);
  and and_2 (and_2_out, S, B);
  or or_1 (Y, and_1_out, and_2_out);

  // Notes on the sheet:
  //   2X1 MULTIPLEXER
endmodule
