// Logisim project B-12.circ as structural Verilog: 1 circuit, main circuit main
module main (
  input  X0,
  input  X1,
  input  X2,
  input  X0_2,
  input  X1_2,
  input  X2_2,
  input  Y___nX2,
  input  X1_3,
  input  X2_3,
  input  Y___X2,
  input  X1_4,
  input  X2_4,
  output out_13,
  output out_14,
  output Y,
  output Y_2
);

  wire and_1_out, and_2_out, and_3_out, and_4_out, and_5_out, and_6_out, not_1_out, not_2_out, not_3_out,
       not_4_out, not_5_out, not_6_out;

  not not_1 (not_1_out, X0);
  not not_2 (not_2_out, X1);
  not not_3 (not_3_out, X2);
  not not_4 (not_4_out, X0_2);
  not not_5 (not_5_out, X1_2);
  not not_6 (not_6_out, X2_2);
  not not_7 (Y, X2_3);
  and and_1 (and_1_out, X0, X1, not_3_out);
  and and_2 (and_2_out, X0, not_2_out, X2);
  and and_3 (and_3_out, X2, X1, not_1_out);
  and and_4 (and_4_out, X0_2, not_5_out, not_6_out);
  and and_5 (and_5_out, X1_2, not_6_out, not_4_out);
  and and_6 (and_6_out, not_4_out, not_5_out, X2_2);
  or or_1 (out_13, and_1_out, and_2_out, and_3_out);
  or or_2 (out_14, and_4_out, and_5_out, and_6_out);

  assign Y_2 = X2_4;

  // Notes on the sheet:
  //   X0
  //   X0
  //   Y = ~X2.X1.X0 + X2.~X1.X0 + X2.X1.~X0
  //   Y = ~X2.~X1.X0 + ~X2.X1.~X0 + X2.~X1.~X0
endmodule
