// Logisim project B-13.circ as structural Verilog
module _3_Bit_Signed_Less_Than (
  input  [2:0] X,
  input  [2:0] Y,
  output LT
);

  wire and_1_out, and_2_out, and_3_out, and_4_out, and_5_out, not_1_out, not_2_out, not_3_out, xnor_1_out,
       xnor_2_out;

  not not_1 (not_1_out, X[0]);
  and and_1 (and_1_out, not_1_out, Y[0]);
  not not_2 (not_2_out, X[1]);
  and and_2 (and_2_out, not_2_out, Y[1]);
  and and_3 (and_3_out, X[2], not_3_out);
  not not_3 (not_3_out, Y[2]);
  xnor xnor_1 (xnor_1_out, X[1], Y[1]);
  xnor xnor_2 (xnor_2_out, X[2], Y[2]);
  and and_4 (and_4_out, and_1_out, xnor_1_out, xnor_2_out);
  and and_5 (and_5_out, and_2_out, xnor_2_out);
  or or_1 (LT, and_4_out, and_5_out, and_3_out);

  // Notes on the sheet:
  //   x0 < y0
  //   x1 < y1
  //   x2 > y2
  //   x1 == y1
  //   x2 == y2
  //   3 bit Less than signed function
endmodule

module _6_Bit_Unsigned_Less_Than (
  input  [5:0] X,
  input  [5:0] Y,
  output out_3
);

  wire n3_bit_unsigned_less_than_1_lt;

  _3_Bit_Unsigned_Less_Than u_3_bit_unsigned_less_than_1 (
    .X(X[5:3]), .Y(Y[5:3]), .MSB_LT(1'b0), .LT(n3_bit_unsigned_less_than_1_lt));
  _3_Bit_Unsigned_Less_Than u_3_bit_unsigned_less_than_2 (
    .X(X[2:0]), .Y(Y[2:0]), .MSB_LT(n3_bit_unsigned_less_than_1_lt), .LT(out_3));

  // Notes on the sheet:
  //   6 bit Less than unsigned function
endmodule

module _3_Bit_Unsigned_Less_Than (
  input  [2:0] X,
  input  [2:0] Y,
  input  MSB_LT,
  output LT
);

  wire and_1_out, and_2_out, and_3_out, and_4_out, and_5_out, not_1_out, not_2_out, not_3_out, xnor_1_out,
       xnor_2_out;

  not not_1 (not_1_out, X[0]);
  and and_1 (and_1_out, not_1_out, Y[0]);
  not not_2 (not_2_out, X[1]);
  and and_2 (and_2_out, not_2_out, Y[1]);
  not not_3 (not_3_out, X[2]);
  and and_3 (and_3_out, not_3_out, Y[2]);
  xnor xnor_1 (xnor_1_out, X[1], Y[1]);
  xnor xnor_2 (xnor_2_out, X[2], Y[2]);
  and and_4 (and_4_out, and_1_out, xnor_1_out, xnor_2_out);
  and and_5 (and_5_out, and_2_out, xnor_2_out);
  or or_1 (LT, and_4_out, and_5_out, and_3_out, MSB_LT);

  // Notes on the sheet:
  //   x0 < y0
  //   x1 < y1
  //   x2 < y2
  //   x1 == y1
  //   x2 == y2
  //   3 bit Less than unsigned function
endmodule

module _6_Bit_Signed_Less_Than (
  input  [5:0] X,
  input  [5:0] Y,
  output out_3
);

  wire n3_bit_signed_less_than_1_lt;

  _3_Bit_Signed_Less_Than u_3_bit_signed_less_than_1 (.X(X[5:3]), .Y(Y[5:3]), .LT(n3_bit_signed_less_than_1_lt));
  _3_Bit_Unsigned_Less_Than u_3_bit_unsigned_less_than_1 (
    .X(X[2:0]), .Y(Y[2:0]), .MSB_LT(n3_bit_signed_less_than_1_lt), .LT(out_3));

  // Notes on the sheet:
  //   6 bit Less than signed function
endmodule

module _3_Bit_Equal (
  input  [2:0] X,
  input  [2:0] Y,
  output out_3
);

  wire xnor_1_out, xnor_2_out, xnor_3_out;

  xnor xnor_1 (xnor_1_out, X[0], Y[0]);
  xnor xnor_2 (xnor_2_out, X[1], Y[1]);
  xnor xnor_3 (xnor_3_out, X[2], Y[2]);
  and and_1 (out_3, xnor_1_out, xnor_2_out, xnor_3_out);

  // Notes on the sheet:
  //   3 bit equal function
endmodule
