// Logisim project B-14.circ as structural Verilog: 1 circuit, main circuit main
module main (
  input  A,
  input  B,
  input  S,
  output C,
  output D
);

  wire and_1_out, and_2_out, and_3_out, and_4_out, not_1_out, not_2_out;

  not not_1 (not_1_out, S);
  not not_2 (not_2_out, S);
  and and_1 (and_1_out, A, S);
  and and_2 (and_2_out, B, not_1_out);
  and and_3 (and_3_out, A, not_2_out);
  and and_4 (and_4_out, B, S);
  or or_1 (C, and_1_out, and_2_out);
  or or_2 (D, and_3_out, and_4_out);

  // Notes on the sheet:
  //   Switching Network
endmodule
