// Logisim project B-36.circ as structural Verilog: 6 circuits, main circuit main
module main (
  input  Read_Address,
  input  Input_Bit_1,
  input  Input_Bit_0,
  input  Clock,
  input  Input_Bit_0_2,
  input  Input_Bit_1_2,
  output Output_Bit_0,
  output Output_Bit_1
);

  wire d_flip_flop_1_out_3, d_flip_flop_2_out_3, d_flip_flop_3_out_3, d_flip_flop_4_out_3;

  D_Flip_Flop d_flip_flop_1 (.in_1(Input_Bit_0), .in_2(Clock), .out_3(d_flip_flop_1_out_3));
  D_Flip_Flop d_flip_flop_2 (.in_1(Input_Bit_0_2), .in_2(Clock), .out_3(d_flip_flop_2_out_3));
  D_Flip_Flop d_flip_flop_3 (.in_1(Input_Bit_1), .in_2(Clock), .out_3(d_flip_flop_3_out_3));
  D_Flip_Flop d_flip_flop_4 (.in_1(Input_Bit_1_2), .in_2(Clock), .out_3(d_flip_flop_4_out_3));
  Multiplexer #(.enable("false")) multiplexer_1 (
    .in0(d_flip_flop_1_out_3), .in1(d_flip_flop_2_out_3), .out(Output_Bit_0), .sel(Read_Address));
  Multiplexer #(.enable("false")) multiplexer_2 (
    .in0(d_flip_flop_3_out_3), .in1(d_flip_flop_4_out_3), .out(Output_Bit_1), .sel(Read_Address));

  // Notes on the sheet:
  //   Bit 0
  //   Bit 0
  //   2 BIT REGISTER FILE
  //   Register 0
  //   Register 1
  //   Bit 1
  //   Bit 1
endmodule

module D_LATCH (
  input  D,
  input  C,
  output Q
);

  wire and_1_out, and_2_out, nor_2_out, not_1_out;

  not not_1 (not_1_out, D);
  and and_1 (and_1_out, not_1_out, C);
  and and_2 (and_2_out, D, C);
  nor nor_1 (Q, and_1_out, nor_2_out);
  nor nor_2 (nor_2_out, Q, and_2_out);

  // Notes on the sheet:
  //   D Latch
endmodule

module D_Flip_Flop (
  input  in_1,
  input  in_2,
  output out_3
);

  wire d_latch_1_q, not_1_out;

  D_LATCH d_latch_1 (.D(in_1), .C(in_2), .Q(d_latch_1_q));
  not not_1 (not_1_out, in_2);
  D_LATCH d_latch_2 (.D(d_latch_1_q), .C(not_1_out), .Q(out_3));

  // Notes on the sheet:
  //   Master
  //   D Flip Flop
  //   Slave
endmodule

module _4_Bit_LA_Carry (
);

  PGUnit pgunit_1 ();  // open: a, b, G, P
endmodule

module _1_Bit_LA_Carry (
  input  c_0,
  input  a_0,
  input  b_0,
  output c_1,
  output g_1,
  output p_1
);

  wire and_2_out;

  and and_1 (g_1, a_0, b_0);
  or or_1 (p_1, a_0, b_0);
  and and_2 (and_2_out, c_0, p_1);
  or or_2 (c_1, and_2_out, g_1);

  // Notes on the sheet:
  //   1 Bit Look Ahead Carry Unit
endmodule

module PGUnit (
  input  a,
  input  b,
  output G,
  output P
);

  and and_1 (G, a, b);
  or or_1 (P, b, a, a);

  // Notes on the sheet:
  //   P and G Unit of Carry Look ahead adder
endmodule
