// Logisim project B-38.circ as structural Verilog: 6 circuits, main circuit main
module main (
  input  Init,
  input  Clock,
  output L,
  output M,
  output R
);

  wire and_2_out, and_5_out, d_flip_flop_1_nq, d_flip_flop_1_q, d_flip_flop_2_nq, d_flip_flop_2_q;

  and and_1 (L, d_flip_flop_1_nq, d_flip_flop_2_nq);
  and and_2 (and_2_out, d_flip_flop_2_q, d_flip_flop_1_nq);
  and and_3 (M, d_flip_flop_2_q, d_flip_flop_1_nq);
  D_Flip_Flop d_flip_flop_1 (
    .Q(d_flip_flop_1_q), .nQ(d_flip_flop_1_nq), .Data_Input(and_2_out), .Initalize(Init), .Clock(Clock));
  and and_4 (R, d_flip_flop_1_q, d_flip_flop_2_nq);
  and and_5 (and_5_out, d_flip_flop_2_nq, d_flip_flop_1_nq);
  D_Flip_Flop d_flip_flop_2 (
    .Q(d_flip_flop_2_q), .nQ(d_flip_flop_2_nq), .Data_Input(and_5_out), .Initalize(Init), .Clock(Clock));

  // Notes on the sheet:
  //   ARTIFICIAL EYE FOR EX B-38
endmodule

module D_LATCH (
  input  D,
  input  C,
  output Q,
  output nQ
);

  wire and_1_out, and_2_out, not_1_out;

  not not_1 (not_1_out, D);
  and and_1 (and_1_out, not_1_out, C);
  and and_2 (and_2_out, D, C);
  nor nor_1 (Q, and_1_out, nQ);
  nor nor_2 (nQ, Q, and_2_out);

  // Notes on the sheet:
  //   D Latch
endmodule

module D_Flip_Flop (
  input  Data_Input,
  input  Initalize,
  input  Clock,
  output Q,
  output nQ
);

  wire and_1_out, and_2_out, d_latch_1_q, not_1_out, not_2_out, or_1_out;

  and and_1 (and_1_out, Data_Input, not_1_out);
  not not_1 (not_1_out, Initalize);
  and and_2 (and_2_out, Initalize, 1'b0);
  or or_1 (or_1_out, and_1_out, and_2_out);
  D_LATCH d_latch_1 (.D(or_1_out), .C(Clock), .Q(d_latch_1_q));  // open: nQ
  not not_2 (not_2_out, Clock);
  D_LATCH d_latch_2 (.D(d_latch_1_q), .C(not_2_out), .Q(Q), .nQ(nQ));

  // Notes on the sheet:
  //   Master
  //   D Flip Flop
  //   Slave
endmodule

module _4_Bit_LA_Carry (
);

  PGUnit pgunit_1 ();  // open: a, b, G, P
endmodule

module _1_Bit_LA_Carry (
  input  c_0,
  input  a_0,
  input  b_0,
  output c_1,
  output g_1,
  output p_1
);

  wire and_2_out;

  and and_1 (g_1, a_0, b_0);
  or or_1 (p_1, a_0, b_0);
  and and_2 (and_2_out, c_0, p_1);
  or or_2 (c_1, and_2_out, g_1);

  // Notes on the sheet:
  //   1 Bit Look Ahead Carry Unit
endmodule

module PGUnit (
  input  a,
  input  b,
  output G,
  output P
);

  and and_1 (G, a, b);
  or or_1 (P, b, a, a);

  // Notes on the sheet:
  //   P and G Unit of Carry Look ahead adder
endmodule
