// Logisim project B-40.circ as structural Verilog: 7 circuits, main circuit main
module main (
  input  in_1,
  input  in_2,
  input  in_3,
  input  in_4,
  output out_5,
  output out_6,
  output out_7
);

  _3_Bit_Grey_Code_Counter u_3_bit_grey_code_counter_1 (
    .Init(in_1), .Inc(in_2), .Clock(in_3), .Reset(in_4), .out_5(out_5), .out_6(out_6), .out_7(out_7));
endmodule

module D_LATCH (
  input  D,
  input  C,
  output Q,
  output nQ
);

  wire and_1_out, and_2_out, not_1_out;

  not not_1 (not_1_out, D);
  and and_1 (and_1_out, not_1_out, C);
  and and_2 (and_2_out, D, C);
  nor nor_1 (Q, and_1_out, nQ);
  nor nor_2 (nQ, Q, and_2_out);

  // Notes on the sheet:
  //   D Latch
endmodule

module D_Flip_Flop (
  input  Data_Input,
  input  Initalize,
  input  Clock,
  output Q,
  output nQ
);

  wire and_1_out, and_2_out, d_latch_1_q, not_1_out, not_2_out, or_1_out;

  and and_1 (and_1_out, Data_Input, not_1_out);
  not not_1 (not_1_out, Initalize);
  and and_2 (and_2_out, Initalize, 1'b0);
  or or_1 (or_1_out, and_1_out, and_2_out);
  D_LATCH d_latch_1 (.D(or_1_out), .C(Clock), .Q(d_latch_1_q));  // open: nQ
  not not_2 (not_2_out, Clock);
  D_LATCH d_latch_2 (.D(d_latch_1_q), .C(not_2_out), .Q(Q), .nQ(nQ));

  // Notes on the sheet:
  //   Master
  //   D Flip Flop
  //   Slave
endmodule

module _4_Bit_LA_Carry (
);

  PGUnit pgunit_1 ();  // open: a, b, G, P
endmodule

module _1_Bit_LA_Carry (
  input  c_0,
  input  a_0,
  input  b_0,
  output c_1,
  output g_1,
  output p_1
);

  wire and_2_out;

  and and_1 (g_1, a_0, b_0);
  or or_1 (p_1, a_0, b_0);
  and and_2 (and_2_out, c_0, p_1);
  or or_2 (c_1, and_2_out, g_1);

  // Notes on the sheet:
  //   1 Bit Look Ahead Carry Unit
endmodule

module PGUnit (
  input  a,
  input  b,
  output G,
  output P
);

  and and_1 (G, a, b);
  or or_1 (P, b, a, a);

  // Notes on the sheet:
  //   P and G Unit of Carry Look ahead adder
endmodule

module _3_Bit_Grey_Code_Counter (
  input  Init,
  input  Inc,
  input  Clock,
  input  Reset,
  output out_5,
  output out_6,
  output out_7
);

  wire and_1_out, and_2_out, and_3_out, and_4_out, and_5_out, and_6_out, and_7_out, and_8_out, and_9_out,
       d_flip_flop_1_nq, d_flip_flop_3_nq, not_1_out, or_1_out, or_2_out, xnor_1_out;

  and and_1 (and_1_out, d_flip_flop_3_nq, out_6, d_flip_flop_1_nq);
  and and_2 (and_2_out, out_5, out_7);
  and and_3 (and_3_out, out_5, out_6);
  or or_1 (or_1_out, and_1_out, and_2_out, and_3_out);
  and and_4 (and_4_out, Inc, Clock);
  not not_1 (not_1_out, Reset);
  and and_5 (and_5_out, or_1_out, not_1_out);
  D_Flip_Flop d_flip_flop_1 (
    .Q(out_5), .nQ(d_flip_flop_1_nq), .Data_Input(and_5_out), .Initalize(Init), .Clock(and_4_out));
  and and_6 (and_6_out, out_6, d_flip_flop_3_nq);
  and and_7 (and_7_out, d_flip_flop_1_nq, out_7);
  or or_2 (or_2_out, and_7_out, and_6_out);
  and and_8 (and_8_out, or_2_out, not_1_out);
  D_Flip_Flop d_flip_flop_2 (.Q(out_6), .Data_Input(and_8_out), .Initalize(Init), .Clock(and_4_out));  // open: nQ
  xnor xnor_1 (xnor_1_out, out_5, out_6);
  and and_9 (and_9_out, xnor_1_out, not_1_out);
  D_Flip_Flop d_flip_flop_3 (
    .Q(out_7), .nQ(d_flip_flop_3_nq), .Data_Input(and_9_out), .Initalize(Init), .Clock(and_4_out));

  // Notes on the sheet:
  //   3 Bit Grey Counter
endmodule
