// Logisim project B-44.circ as structural Verilog
module D_LATCH (
  input  D,
  input  C,
  output Q,
  output nQ
);

  wire and_1_out, and_2_out, not_1_out;

  not not_1 (not_1_out, D);
  and and_1 (and_1_out, not_1_out, C);
  and and_2 (and_2_out, D, C);
  nor nor_1 (Q, and_1_out, nQ);
  nor nor_2 (nQ, Q, and_2_out);

  // Notes on the sheet:
  //   D Latch
endmodule

module D_Flip_Flop (
  input  Data_Input,
  input  Initalize,
  input  Clock,
  output Q,
  output nQ
);

  wire and_1_out, and_2_out, d_latch_1_q, not_1_out, not_2_out, or_1_out;

  and and_1 (and_1_out, Data_Input, not_1_out);
  not not_1 (not_1_out, Initalize);
  and and_2 (and_2_out, Initalize, 1'b0);
  or or_1 (or_1_out, and_1_out, and_2_out);
  D_LATCH d_latch_1 (.D(or_1_out), .C(Clock), .Q(d_latch_1_q));  // open: nQ
  not not_2 (not_2_out, Clock);
  D_LATCH d_latch_2 (.D(d_latch_1_q), .C(not_2_out), .Q(Q), .nQ(nQ));

  // Notes on the sheet:
  //   Master
  //   D Flip Flop
  //   Slave
endmodule

module _4_Bit_LA_Carry (
);

  PGUnit pgunit_1 ();  // open: a, b, G, P
endmodule

module _1_Bit_LA_Carry (
  input  c_0,
  input  a_0,
  input  b_0,
  output c_1,
  output g_1,
  output p_1
);

  wire and_2_out;

  and and_1 (g_1, a_0, b_0);
  or or_1 (p_1, a_0, b_0);
  and and_2 (and_2_out, c_0, p_1);
  or or_2 (c_1, and_2_out, g_1);

  // Notes on the sheet:
  //   1 Bit Look Ahead Carry Unit
endmodule

module PGUnit (
  input  a,
  input  b,
  output G,
  output P
);

  and and_1 (G, a, b);
  or or_1 (P, b, a, a);

  // Notes on the sheet:
  //   P and G Unit of Carry Look ahead adder
endmodule

module _3_Bit_Counter (
  input  Down,
  input  Init,
  input  Inc,
  input  Clock,
  input  Reset,
  output out_6,
  output out_7,
  output out_8
);

  wire and_1_out, and_2_out, and_3_out, and_4_out, and_5_out, and_6_out, and_7_out, d_flip_flop_1_nq,
       d_flip_flop_1_q, d_flip_flop_2_nq, d_flip_flop_2_q, d_flip_flop_3_nq, d_flip_flop_3_q, not_1_out,
       or_1_out, xor_2_out;

  and and_1 (and_1_out, d_flip_flop_1_q, d_flip_flop_2_nq);
  and and_2 (and_2_out, d_flip_flop_3_q, d_flip_flop_2_q, d_flip_flop_1_nq);
  or or_1 (or_1_out, and_2_out, and_1_out, and_3_out);
  and and_3 (and_3_out, d_flip_flop_1_q, d_flip_flop_3_nq);
  and and_4 (and_4_out, Inc, Clock);
  not not_1 (not_1_out, Reset);
  and and_5 (and_5_out, or_1_out, not_1_out);
  xor xor_1 (out_6, Down, d_flip_flop_1_q);
  D_Flip_Flop d_flip_flop_1 (
    .Q(d_flip_flop_1_q), .nQ(d_flip_flop_1_nq), .Data_Input(and_5_out), .Initalize(Init), .Clock(and_4_out));
  xor xor_2 (xor_2_out, d_flip_flop_3_q, d_flip_flop_2_q);
  and and_6 (and_6_out, xor_2_out, not_1_out);
  xor xor_3 (out_7, Down, d_flip_flop_2_q);
  D_Flip_Flop d_flip_flop_2 (
    .Q(d_flip_flop_2_q), .nQ(d_flip_flop_2_nq), .Data_Input(and_6_out), .Initalize(Init), .Clock(and_4_out));
  and and_7 (and_7_out, d_flip_flop_3_nq, not_1_out);
  xor xor_4 (out_8, Down, d_flip_flop_3_q);
  D_Flip_Flop d_flip_flop_3 (
    .Q(d_flip_flop_3_q), .nQ(d_flip_flop_3_nq), .Data_Input(and_7_out), .Initalize(Init), .Clock(and_4_out));

  // Notes on the sheet:
  //   Sc
  //   3 Bit Up/Down Counter
  //   Sb
  //   Sa
endmodule

module _6_Bit_Counter (
  input  in_1,
  input  in_2,
  input  in_3,
  input  in_4,
  input  in_5,
  output B5,
  output B4,
  output B3,
  output B2,
  output B1,
  output B0
);

  wire and_1_out;

  _3_Bit_Counter u_3_bit_counter_1 (
    .Down(in_1), .Init(in_2), .Inc(and_1_out), .Clock(in_4), .Reset(in_5), .out_6(B5), .out_7(B4), .out_8(B3));
  _3_Bit_Counter u_3_bit_counter_2 (
    .Down(in_1), .Init(in_2), .Inc(in_3), .Clock(in_4), .Reset(in_5), .out_6(B2), .out_7(B1), .out_8(B0));
  and and_1 (and_1_out, B2, B1, B0);

  // Notes on the sheet:
  //   6 Bit Up/Down Counter
endmodule

module Traffic_Controller_Rom_Based (
  input  NSCar,
  input  EWCar,
  input  TS,
  input  Init,
  input  Clock,
  output out_6
);

  wire d_flip_flop_2_nq, output_logic_1_ewglight, output_logic_1_ewrlight, output_logic_1_ewylight,
       output_logic_1_nsglight, output_logic_1_nsrlight, output_logic_1_nsylight;
  wire [1:0] d_flip_flop_2_q, rom_1_data;

  D_Flip_Flop d_flip_flop_1 (
    .Q(d_flip_flop_2_q[1]), .Data_Input(rom_1_data[1]), .Initalize(Init), .Clock(Clock));  // open: nQ
  ROM #(.addrWidth(5), .dataWidth(2)) rom_1 (
    .addr({TS, EWCar, NSCar, d_flip_flop_2_q}), .data(rom_1_data));  // open: sel
  D_Flip_Flop d_flip_flop_2 (
    .Q(d_flip_flop_2_q[0]), .nQ(d_flip_flop_2_nq), .Data_Input(rom_1_data[0]), .Initalize(Init), .Clock(Clock));
  Output_Logic output_logic_1 (
    .TR(out_6), .NSGLight(output_logic_1_nsglight), .NSYLight(output_logic_1_nsylight),
    .NSRLight(output_logic_1_nsrlight), .EWGLight(output_logic_1_ewglight),
    .EWYLight(output_logic_1_ewylight), .EWRLight(output_logic_1_ewrlight), .S0(d_flip_flop_2_q[1]),
    .S1(d_flip_flop_2_q[0]));
  LED led_1 (.in(output_logic_1_nsrlight));
  LED led_2 (.in(output_logic_1_nsylight));
  LED led_3 (.in(output_logic_1_nsglight));
  LED led_4 (.in(output_logic_1_ewrlight));
  LED led_5 (.in(output_logic_1_ewylight));
  LED led_6 (.in(output_logic_1_ewglight));

  // Notes on the sheet:
  //   S0
  //   Traffic Controller ROM Based
  //   contents of rom_1 (hex, n*v repeats v):
  //   0 3 0 3 0 3 0 3 0 3 0 3 0 3 0 3 0 3 0 3 0 3 0 2 1 3 0 3 1 3 0 2
  //   S1
  //   NS LIGHTS
endmodule

module Next_State_Logic (
  input  TS,
  input  EWCar,
  input  NSCar,
  input  S0,
  input  S1,
  output S1_plus,
  output S0_plus
);

  wire and_1_out, and_2_out, and_3_out, and_4_out, not_1_out, not_2_out, not_3_out;

  not not_1 (not_1_out, TS);
  not not_2 (not_2_out, S0);
  not not_3 (not_3_out, NSCar);
  and and_1 (and_1_out, not_1_out, S1);
  and and_2 (and_2_out, not_3_out, S1);
  and and_3 (and_3_out, not_2_out, S1);
  and and_4 (and_4_out, TS, EWCar, not_2_out);
  or or_1 (S1_plus, and_1_out, and_2_out, and_3_out, and_4_out);

  assign S0_plus = S1;
endmodule

module Output_Logic (
  input  S0,
  input  S1,
  output TR,
  output NSGLight,
  output NSYLight,
  output NSRLight,
  output EWGLight,
  output EWYLight,
  output EWRLight
);

  wire not_2_out;

  not not_1 (EWRLight, S0);
  not not_2 (not_2_out, S1);
  xnor xnor_1 (TR, S0, S1);
  and and_1 (NSGLight, EWRLight, not_2_out);
  and and_2 (NSYLight, EWRLight, S1);
  and and_3 (EWGLight, S0, S1);
  and and_4 (EWYLight, S0, not_2_out);

  assign NSRLight = S0;

  // Notes on the sheet:
  //   Traffic Controller Output Logic
endmodule

module Traffice_Controller (
  input  TS,
  input  EWCar,
  input  NSCar,
  input  Init,
  input  Clock,
  output out_6
);

  wire d_flip_flop_1_q, d_flip_flop_2_q, next_state_logic_1_s0_plus, next_state_logic_1_s1_plus,
       output_logic_1_ewglight, output_logic_1_ewrlight, output_logic_1_ewylight, output_logic_1_nsglight,
       output_logic_1_nsrlight, output_logic_1_nsylight;

  Next_State_Logic next_state_logic_1 (
    .S1_plus(next_state_logic_1_s1_plus), .S0_plus(next_state_logic_1_s0_plus), .TS(TS), .EWCar(EWCar),
    .NSCar(NSCar), .S0(d_flip_flop_1_q), .S1(d_flip_flop_2_q));
  D_Flip_Flop d_flip_flop_1 (
    .Q(d_flip_flop_1_q), .Data_Input(next_state_logic_1_s0_plus), .Initalize(Init), .Clock(Clock));  // open: nQ
  D_Flip_Flop d_flip_flop_2 (
    .Q(d_flip_flop_2_q), .Data_Input(next_state_logic_1_s1_plus), .Initalize(Init), .Clock(Clock));  // open: nQ
  Output_Logic output_logic_1 (
    .TR(out_6), .NSGLight(output_logic_1_nsglight), .NSYLight(output_logic_1_nsylight),
    .NSRLight(output_logic_1_nsrlight), .EWGLight(output_logic_1_ewglight),
    .EWYLight(output_logic_1_ewylight), .EWRLight(output_logic_1_ewrlight), .S0(d_flip_flop_1_q),
    .S1(d_flip_flop_2_q));
  LED led_1 (.in(output_logic_1_nsrlight));
  LED led_2 (.in(output_logic_1_nsylight));
  LED led_3 (.in(output_logic_1_nsglight));
  LED led_4 (.in(output_logic_1_ewrlight));
  LED led_5 (.in(output_logic_1_ewylight));
  LED led_6 (.in(output_logic_1_ewglight));

  // Notes on the sheet:
  //   S0
  //   Traffic Controller
  //   S1
  //   NS LIGHTS
  //   EWLIGHTS
endmodule
