// Logisim project B-5.circ as structural Verilog: 1 circuit, main circuit main
module main (
  input  A,
  input  B,
  input  A_2,
  input  A_3,
  input  B_2,
  output out_6,
  output out_7,
  output out_8
);

  wire nor_1_out, nor_2_out, nor_3_out;

  nor nor_1 (nor_1_out, A_3, A_3);
  nor nor_2 (nor_2_out, B_2, B_2);
  nor nor_3 (nor_3_out, A, B);
  nor nor_4 (out_7, A_2, A_2);
  nor nor_5 (out_6, nor_3_out, nor_3_out);
  nor nor_6 (out_8, nor_1_out, nor_2_out);

  // Notes on the sheet:
  //   OR GATE USING NOR GATE
  //   NOT GATE USING NOR GATE
  //   AND GATE USING NOR GATE
endmodule
