// Logisim project B-6.circ as structural Verilog: 1 circuit, main circuit main
module main (
  input  A,
  input  B,
  input  A_2,
  input  A_3,
  input  B_2,
  output out_6,
  output out_7,
  output out_8
);

  wire nand_1_out, nand_2_out, nand_3_out;

  nand nand_1 (nand_1_out, A_3, A_3);
  nand nand_2 (nand_2_out, B_2, B_2);
  nand nand_3 (nand_3_out, A, B);
  nand nand_4 (out_7, A_2, A_2);
  nand nand_5 (out_6, nand_3_out, nand_3_out);
  nand nand_6 (out_8, nand_1_out, nand_2_out);

  // Notes on the sheet:
  //   AND GATE USING NAND GATE
  //   NOT GATE USING NAND GATE
  //   OR GATE USING NAND GATE
endmodule
