// Logisim project B-8.circ as structural Verilog: 1 circuit, main circuit main
module main (
  input  A,
  input  B,
  input  C,
  input  D,
  input  A_2,
  input  B_2,
  input  C_2,
  input  D_2,
  output Y,
  output Y_2
);

  wire and_1_out, and_2_out, and_3_out, and_4_out, and_5_out, and_6_out, not_1_out, not_2_out, not_3_out,
       not_4_out, not_5_out, not_6_out, or_1_out, or_2_out, xor_1_out, xor_2_out;

  not not_1 (not_1_out, A_2);
  not not_2 (not_2_out, B_2);
  not not_3 (not_3_out, C_2);
  not not_4 (not_4_out, D_2);
  xor xor_1 (xor_1_out, A, B);
  xor xor_2 (xor_2_out, C, D);
  and and_1 (and_1_out, not_1_out, B_2);
  and and_2 (and_2_out, A_2, not_2_out);
  and and_3 (and_3_out, not_3_out, D_2);
  and and_4 (and_4_out, C_2, not_4_out);
  xor xor_3 (Y, xor_1_out, xor_2_out);
  or or_1 (or_1_out, and_1_out, and_2_out);
  or or_2 (or_2_out, and_3_out, and_4_out);
  not not_5 (not_5_out, or_1_out);
  not not_6 (not_6_out, or_2_out);
  and and_5 (and_5_out, not_5_out, or_2_out);
  and and_6 (and_6_out, or_1_out, not_6_out);
  or or_3 (Y_2, and_5_out, and_6_out);

  // Notes on the sheet:
  //   ODD PARITY FUNCTION USING XOR GATES
  //   Y = (A XOR B) XOR (C XOR D)
  //   ODD PARITY FUNCTION USING AND OR NOT GATES
  //   LOGIC EQUATION FOR 4 INPUT ODD PARITY FUNCTION
endmodule
